// Logisim project Coordinate_Tracker.circ as structural Verilog: 19 circuits, main circuit View
module View (
  input  Face_North,
  input  Face_west,
  input  Face_East,
  input  Face_South,
  output Facing_North,
  output Facing_West,
  output Facing_East,
  output Facing_South
);

  wire direction_logic_1_eo, direction_logic_1_no, direction_logic_1_so, direction_logic_1_wo, or_1_out,
       or_2_out, or_3_out, or_4_out;

  Direction_logic direction_logic_1 (
    .n(Face_North), .w(Face_west), .e(Face_East), .s(Face_South), .No(direction_logic_1_no),
    .Wo(direction_logic_1_wo), .Eo(direction_logic_1_eo), .So(direction_logic_1_so));
  D_Flip_Flop u_Facing_North (
    .D(direction_logic_1_no), .Q(Facing_North), .preset(direction_logic_1_no), .reset(or_1_out));  // open: clk, Qn, en
  or or_1 (or_1_out, direction_logic_1_wo, direction_logic_1_eo, direction_logic_1_so);
  D_Flip_Flop u_Facing_West (
    .D(direction_logic_1_wo), .Q(Facing_West), .preset(direction_logic_1_wo), .reset(or_2_out));  // open: clk, Qn, en
  or or_2 (or_2_out, direction_logic_1_no, direction_logic_1_eo, direction_logic_1_so);
  D_Flip_Flop u_Facing_East (
    .D(direction_logic_1_eo), .Q(Facing_East), .preset(direction_logic_1_eo), .reset(or_3_out));  // open: clk, Qn, en
  or or_3 (or_3_out, direction_logic_1_no, direction_logic_1_wo, direction_logic_1_so);
  D_Flip_Flop u_Facing_South (
    .D(direction_logic_1_so), .Q(Facing_South), .preset(direction_logic_1_so), .reset(or_4_out));  // open: clk, Qn, en
  or or_4 (or_4_out, direction_logic_1_eo, direction_logic_1_wo, direction_logic_1_no);
endmodule

module Direction_logic (
  input  n,
  input  w,
  input  e,
  input  s,
  output No,
  output Wo,
  output Eo,
  output So
);

  wire not_1_out, not_2_out, not_3_out, not_4_out, not_5_out, not_6_out, not_7_out, not_8_out, not_9_out,
       not_10_out, not_11_out, not_12_out;

  not not_1 (not_1_out, w);
  not not_2 (not_2_out, e);
  not not_3 (not_3_out, s);
  not not_4 (not_4_out, n);
  not not_5 (not_5_out, e);
  not not_6 (not_6_out, s);
  not not_7 (not_7_out, n);
  not not_8 (not_8_out, w);
  not not_9 (not_9_out, s);
  not not_10 (not_10_out, n);
  not not_11 (not_11_out, w);
  not not_12 (not_12_out, e);
  and and_1 (No, n, not_1_out, not_2_out, not_3_out);
  and and_2 (Wo, not_4_out, w, not_5_out, not_6_out);
  and and_3 (Eo, not_7_out, not_8_out, e, not_9_out);
  and and_4 (So, not_10_out, not_11_out, not_12_out, s);
endmodule

module main (
  input  Increment,
  input  Reset,
  input  N,
  input  W,
  input  E,
  input  S,
  output [9:0] y_axis,
  output [9:0] y_axis_2,
  output N_2,
  output W_2,
  output E_2,
  output [9:0] North,
  output [11:0] Total_Steps,
  output S_2,
  output [9:0] West,
  output [9:0] East,
  output [9:0] South
);

  wire or_1_out;

  or or_1 (or_1_out, N, Reset);
  View view_1 (
    .Face_North(or_1_out), .Face_west(W), .Face_East(E), .Face_South(S), .Facing_North(N_2),
    .Facing_West(W_2), .Facing_East(E_2), .Facing_South(S_2));
  Directions directions_1 (
    .N(N_2), .W(W_2), .E(E_2), .S(S_2), .I(Increment), .Reset(Reset), .No(North), .Wo(West), .Eo(East),
    .So(South));
  Totall_steps totall_steps_1 (.in_1(North), .in_2(West), .in_3(East), .in_4(South), .out_5(Total_Steps));
  Subtractor #(.width(10)) subtractor_1 (.a(North), .b(South), .out(y_axis));  // open: bin, bout
  Subtractor #(.width(10)) subtractor_2 (.a(East), .b(West), .out(y_axis_2));  // open: bin, bout

  // Notes on the sheet:
  //   change direction
  //   current direction
  //   distance traveled in each direction
endmodule

module Stepper_A (
  input  Reset,
  input  N,
  input  W,
  input  E,
  input  S,
  input  I,
  output [7:0] Y_axis,
  output [7:0] X_axis
);

  Counter counter_1 (
    .Enable_direction(N), .Take_step(I), .Enable_direction_of_oppasite(S), .Reset(Reset), .out_5(Y_axis));
  Counter counter_2 (
    .Enable_direction(E), .Take_step(I), .Enable_direction_of_oppasite(W), .Reset(Reset), .out_5(X_axis));
endmodule

module Counter (
  input  Enable_direction,
  input  Take_step,
  input  Enable_direction_of_oppasite,
  input  Reset,
  output [7:0] out_5
);

  wire and_1_out, and_2_out, and_3_out, and_4_out, and_5_out, and_6_out, and_7_out, and_8_out, and_9_out,
       and_10_out, and_11_out, and_12_out, and_13_out, and_14_out, and_15_out, and_16_out, and_17_out,
       and_18_out, or_1_out, or_2_out, or_3_out, or_4_out, or_5_out, or_6_out, or_7_out, or_8_out, or_9_out,
       tiny_counter_negative_1_f, tiny_counter_negative_1_f6, tiny_counter_negative_1_f7,
       tiny_counter_negative_1_f8, tiny_counter_negative_1_g, tiny_counter_negative_1_h,
       tiny_counter_negative_1_i, tiny_counter_negative_1_j, tiny_counter_positive_1_f,
       tiny_counter_positive_1_f6, tiny_counter_positive_1_f7, tiny_counter_positive_1_f8,
       tiny_counter_positive_1_g, tiny_counter_positive_1_h, tiny_counter_positive_1_i,
       tiny_counter_positive_1_j;

  and and_1 (and_1_out, Enable_direction, Take_step);
  and and_2 (and_2_out, Take_step, Enable_direction_of_oppasite);
  or or_1 (or_1_out, and_1_out, and_2_out);
  Tiny_counter_Positive tiny_counter_positive_1 (
    .a(out_5[7]), .b(out_5[6]), .c(out_5[5]), .d(out_5[4]), .e(out_5[3]), .a6(out_5[2]), .a7(out_5[1]),
    .a8(out_5[0]), .f(tiny_counter_positive_1_f), .g(tiny_counter_positive_1_g),
    .h(tiny_counter_positive_1_h), .i(tiny_counter_positive_1_i), .j(tiny_counter_positive_1_j),
    .f6(tiny_counter_positive_1_f6), .f7(tiny_counter_positive_1_f7), .f8(tiny_counter_positive_1_f8));
  or or_2 (or_2_out, and_3_out, and_4_out);
  and and_3 (and_3_out, Enable_direction, tiny_counter_positive_1_f);
  and and_4 (and_4_out, Enable_direction_of_oppasite, tiny_counter_negative_1_f);
  D_Flip_Flop d_ff_1 (.clk(or_1_out), .D(or_2_out), .Q(out_5[7]), .reset(Reset));  // open: Qn, preset, en
  Tiny_counter_negative tiny_counter_negative_1 (
    .a(out_5[7]), .b(out_5[6]), .c(out_5[5]), .d(out_5[4]), .e(out_5[3]), .a6(out_5[2]), .a7(out_5[1]),
    .a8(out_5[0]), .f(tiny_counter_negative_1_f), .g(tiny_counter_negative_1_g),
    .h(tiny_counter_negative_1_h), .i(tiny_counter_negative_1_i), .j(tiny_counter_negative_1_j),
    .f6(tiny_counter_negative_1_f6), .f7(tiny_counter_negative_1_f7), .f8(tiny_counter_negative_1_f8));
  or or_3 (or_3_out, and_5_out, and_6_out);
  and and_5 (and_5_out, Enable_direction, tiny_counter_positive_1_g);
  and and_6 (and_6_out, Enable_direction_of_oppasite, tiny_counter_negative_1_g);
  D_Flip_Flop d_ff_2 (.clk(or_1_out), .D(or_3_out), .Q(out_5[6]), .reset(Reset));  // open: Qn, preset, en
  or or_4 (or_4_out, and_7_out, and_8_out);
  and and_7 (and_7_out, Enable_direction, tiny_counter_positive_1_h);
  and and_8 (and_8_out, Enable_direction_of_oppasite, tiny_counter_negative_1_h);
  D_Flip_Flop d_ff_3 (.clk(or_1_out), .D(or_4_out), .Q(out_5[5]), .reset(Reset));  // open: Qn, preset, en
  or or_5 (or_5_out, and_9_out, and_10_out);
  and and_9 (and_9_out, Enable_direction, tiny_counter_positive_1_i);
  and and_10 (and_10_out, Enable_direction_of_oppasite, tiny_counter_negative_1_i);
  D_Flip_Flop d_ff_4 (.clk(or_1_out), .D(or_5_out), .Q(out_5[4]), .reset(Reset));  // open: Qn, preset, en
  or or_6 (or_6_out, and_11_out, and_12_out);
  and and_11 (and_11_out, Enable_direction, tiny_counter_positive_1_j);
  D_Flip_Flop d_ff_5 (.clk(or_1_out), .D(or_6_out), .Q(out_5[3]), .reset(Reset));  // open: Qn, preset, en
  and and_12 (and_12_out, Enable_direction_of_oppasite, tiny_counter_negative_1_j);
  or or_7 (or_7_out, and_13_out, and_14_out);
  and and_13 (and_13_out, Enable_direction, tiny_counter_positive_1_f6);
  and and_14 (and_14_out, Enable_direction_of_oppasite, tiny_counter_negative_1_f6);
  D_Flip_Flop d_ff_6 (.clk(or_1_out), .D(or_7_out), .Q(out_5[2]), .reset(Reset));  // open: Qn, preset, en
  and and_15 (and_15_out, Enable_direction, tiny_counter_positive_1_f7);
  D_Flip_Flop d_ff_7 (.clk(or_1_out), .D(or_8_out), .Q(out_5[1]), .reset(Reset));  // open: Qn, preset, en
  or or_8 (or_8_out, and_15_out, and_16_out);
  and and_16 (and_16_out, Enable_direction_of_oppasite, tiny_counter_negative_1_f7);
  or or_9 (or_9_out, and_17_out, and_18_out);
  and and_17 (and_17_out, Enable_direction, tiny_counter_positive_1_f8);
  D_Flip_Flop d_ff_8 (.clk(or_1_out), .D(or_9_out), .Q(out_5[0]), .reset(Reset));  // open: Qn, preset, en
  and and_18 (and_18_out, Enable_direction_of_oppasite, tiny_counter_negative_1_f8);
endmodule

module Tiny_counter_Positive (
  input  a,
  input  b,
  input  c,
  input  d,
  input  e,
  input  a6,
  input  a7,
  input  a8,
  output f,
  output g,
  output h,
  output i,
  output j,
  output f6,
  output f7,
  output f8
);

  wire and_1_out, and_2_out, and_3_out, and_4_out, and_5_out, and_6_out, and_7_out, and_8_out, and_9_out,
       and_10_out, and_11_out, and_12_out, and_13_out, and_14_out, and_15_out, and_16_out, and_17_out,
       and_18_out, and_19_out, and_20_out, and_21_out, and_22_out, and_23_out, and_24_out, and_25_out,
       and_26_out, and_27_out, and_28_out, and_29_out, and_30_out, and_31_out, and_32_out, and_33_out,
       and_34_out, and_35_out, not_1_out, not_2_out, not_3_out, not_4_out, not_5_out, not_6_out, not_7_out,
       not_8_out, not_9_out, not_10_out, not_11_out, not_12_out, not_13_out, not_14_out, not_15_out,
       not_16_out, not_17_out, not_18_out, not_19_out, not_20_out, not_21_out, not_22_out, not_23_out,
       not_24_out, not_25_out, not_26_out, not_27_out, not_28_out, not_29_out, not_30_out, not_31_out,
       not_32_out, not_33_out, not_34_out, not_35_out;

  not not_1 (not_1_out, a);
  not not_2 (not_2_out, b);
  not not_3 (not_3_out, c);
  not not_4 (not_4_out, d);
  not not_5 (not_5_out, e);
  not not_6 (not_6_out, a6);
  not not_7 (not_7_out, a7);
  not not_8 (not_8_out, a8);
  not not_9 (not_9_out, b);
  not not_10 (not_10_out, c);
  not not_11 (not_11_out, d);
  not not_12 (not_12_out, e);
  not not_13 (not_13_out, a6);
  not not_14 (not_14_out, a7);
  not not_15 (not_15_out, a8);
  not not_16 (not_16_out, c);
  not not_17 (not_17_out, d);
  not not_18 (not_18_out, e);
  not not_19 (not_19_out, a6);
  not not_20 (not_20_out, a7);
  not not_21 (not_21_out, a8);
  not not_22 (not_22_out, d);
  not not_23 (not_23_out, e);
  not not_24 (not_24_out, a6);
  not not_25 (not_25_out, a7);
  not not_26 (not_26_out, a8);
  not not_27 (not_27_out, e);
  not not_28 (not_28_out, a6);
  not not_29 (not_29_out, a7);
  not not_30 (not_30_out, a8);
  not not_31 (not_31_out, a6);
  and and_1 (and_1_out, not_31_out, a7, a8);
  and and_2 (and_2_out, a6, not_32_out);
  not not_32 (not_32_out, a7);
  and and_3 (and_3_out, a6, not_33_out);
  not not_33 (not_33_out, a8);
  not not_34 (not_34_out, a7);
  and and_4 (and_4_out, not_34_out, a8);
  and and_5 (and_5_out, a7, not_35_out);
  not not_35 (not_35_out, a8);
  not not_36 (f8, a8);
  and and_6 (and_6_out, not_1_out, b, c, d, e, a6, a7, a8);
  and and_7 (and_7_out, a, not_2_out);
  and and_8 (and_8_out, a, not_3_out);
  and and_9 (and_9_out, a, not_4_out);
  and and_10 (and_10_out, a, not_5_out);
  and and_11 (and_11_out, a, not_6_out);
  and and_12 (and_12_out, a, not_7_out);
  and and_13 (and_13_out, a, not_8_out);
  and and_14 (and_14_out, not_9_out, c, d, e, a6, a7, a8);
  and and_15 (and_15_out, b, not_10_out);
  and and_16 (and_16_out, b, not_11_out);
  and and_17 (and_17_out, b, not_12_out);
  and and_18 (and_18_out, b, not_13_out);
  and and_19 (and_19_out, b, not_14_out);
  and and_20 (and_20_out, b, not_15_out);
  and and_21 (and_21_out, not_16_out, d, e, a6, a7, a8);
  and and_22 (and_22_out, c, not_17_out);
  and and_23 (and_23_out, c, not_18_out);
  and and_24 (and_24_out, c, not_19_out);
  and and_25 (and_25_out, c, not_20_out);
  and and_26 (and_26_out, c, not_21_out);
  and and_27 (and_27_out, not_22_out, e, a6, a7, a8);
  and and_28 (and_28_out, d, not_23_out);
  and and_29 (and_29_out, d, not_24_out);
  and and_30 (and_30_out, d, not_25_out);
  and and_31 (and_31_out, d, not_26_out);
  and and_32 (and_32_out, not_27_out, a6, a7, a8);
  and and_33 (and_33_out, e, not_28_out);
  and and_34 (and_34_out, e, not_29_out);
  and and_35 (and_35_out, e, not_30_out);
  or or_1 (f6, and_1_out, and_2_out, and_3_out);
  or or_2 (f7, and_4_out, and_5_out);
  or or_3 (f, and_6_out, and_7_out, and_8_out, and_9_out, and_10_out, and_11_out, and_12_out, and_13_out);
  or or_4 (g, and_14_out, and_15_out, and_16_out, and_17_out, and_18_out, and_19_out, and_20_out);
  or or_5 (h, and_21_out, and_22_out, and_23_out, and_24_out, and_25_out, and_26_out);
  or or_6 (i, and_27_out, and_28_out, and_29_out, and_30_out, and_31_out);
  or or_7 (j, and_32_out, and_33_out, and_34_out, and_35_out);
endmodule

module Tiny_counter_negative (
  input  a,
  input  b,
  input  c,
  input  d,
  input  e,
  input  a6,
  input  a7,
  input  a8,
  output f,
  output g,
  output h,
  output i,
  output j,
  output f6,
  output f7,
  output f8
);

  wire and_1_out, and_2_out, and_3_out, and_4_out, and_5_out, and_6_out, and_7_out, and_8_out, and_9_out,
       and_10_out, and_11_out, and_12_out, and_13_out, and_14_out, and_15_out, and_16_out, and_17_out,
       and_18_out, and_19_out, and_20_out, and_21_out, and_22_out, and_23_out, and_24_out, and_25_out,
       and_26_out, and_27_out, and_28_out, and_29_out, and_30_out, and_31_out, and_32_out, and_33_out,
       and_34_out, and_35_out, not_1_out, not_2_out, not_3_out, not_4_out, not_5_out, not_6_out, not_7_out,
       not_8_out, not_9_out, not_10_out, not_11_out, not_12_out, not_13_out, not_14_out, not_15_out,
       not_16_out, not_17_out, not_18_out, not_19_out, not_20_out, not_21_out, not_22_out, not_23_out,
       not_24_out, not_25_out, not_26_out, not_27_out, not_28_out, not_29_out, not_30_out, not_31_out,
       not_32_out, not_33_out, not_34_out, not_35_out;

  not not_1 (not_1_out, a);
  not not_2 (not_2_out, b);
  not not_3 (not_3_out, c);
  not not_4 (not_4_out, d);
  not not_5 (not_5_out, e);
  not not_6 (not_6_out, a6);
  not not_7 (not_7_out, a7);
  not not_8 (not_8_out, a8);
  not not_9 (not_9_out, b);
  not not_10 (not_10_out, c);
  not not_11 (not_11_out, d);
  not not_12 (not_12_out, e);
  not not_13 (not_13_out, a6);
  not not_14 (not_14_out, a7);
  not not_15 (not_15_out, a8);
  not not_16 (not_16_out, c);
  not not_17 (not_17_out, d);
  not not_18 (not_18_out, e);
  not not_19 (not_19_out, a6);
  not not_20 (not_20_out, a7);
  not not_21 (not_21_out, a8);
  not not_22 (not_22_out, d);
  not not_23 (not_23_out, e);
  not not_24 (not_24_out, a6);
  not not_25 (not_25_out, a7);
  not not_26 (not_26_out, a8);
  not not_27 (not_27_out, e);
  not not_28 (not_28_out, a6);
  not not_29 (not_29_out, a7);
  not not_30 (not_30_out, a8);
  not not_31 (not_31_out, a6);
  not not_32 (not_32_out, a7);
  and and_1 (and_1_out, not_31_out, not_32_out, not_33_out);
  not not_33 (not_33_out, a8);
  and and_2 (and_2_out, a6, a8);
  and and_3 (and_3_out, a6, a7);
  not not_34 (not_34_out, a7);
  and and_4 (and_4_out, not_34_out, not_35_out);
  not not_35 (not_35_out, a8);
  and and_5 (and_5_out, a7, a8);
  not not_36 (f8, a8);
  and and_6 (and_6_out, not_1_out, not_2_out, not_3_out, not_4_out, not_5_out, not_6_out, not_7_out, not_8_out);
  and and_7 (and_7_out, a, a8);
  and and_8 (and_8_out, a, a7);
  and and_9 (and_9_out, a, a6);
  and and_10 (and_10_out, a, e);
  and and_11 (and_11_out, a, d);
  and and_12 (and_12_out, a, c);
  and and_13 (and_13_out, a, b);
  and and_14 (and_14_out, not_9_out, not_10_out, not_11_out, not_12_out, not_13_out, not_14_out, not_15_out);
  and and_15 (and_15_out, b, a8);
  and and_16 (and_16_out, b, a7);
  and and_17 (and_17_out, b, a6);
  and and_18 (and_18_out, b, e);
  and and_19 (and_19_out, b, d);
  and and_20 (and_20_out, b, c);
  and and_21 (and_21_out, not_16_out, not_17_out, not_18_out, not_19_out, not_20_out, not_21_out);
  and and_22 (and_22_out, c, a8);
  and and_23 (and_23_out, c, a7);
  and and_24 (and_24_out, c, a6);
  and and_25 (and_25_out, c, e);
  and and_26 (and_26_out, c, d);
  and and_27 (and_27_out, not_22_out, not_23_out, not_24_out, not_25_out, not_26_out);
  and and_28 (and_28_out, d, a8);
  and and_29 (and_29_out, d, a7);
  and and_30 (and_30_out, d, a6);
  and and_31 (and_31_out, d, e);
  and and_32 (and_32_out, not_27_out, not_28_out, not_29_out, not_30_out);
  and and_33 (and_33_out, e, a8);
  and and_34 (and_34_out, e, a7);
  and and_35 (and_35_out, e, a6);
  or or_1 (f6, and_1_out, and_2_out, and_3_out);
  or or_2 (f7, and_4_out, and_5_out);
  or or_3 (f, and_6_out, and_7_out, and_8_out, and_9_out, and_10_out, and_11_out, and_12_out, and_13_out);
  or or_4 (g, and_14_out, and_15_out, and_16_out, and_17_out, and_18_out, and_19_out, and_20_out);
  or or_5 (h, and_21_out, and_22_out, and_23_out, and_24_out, and_25_out, and_26_out);
  or or_6 (i, and_27_out, and_28_out, and_29_out, and_30_out, and_31_out);
  or or_7 (j, and_32_out, and_33_out, and_34_out, and_35_out);
endmodule

module signer (
  input  [9:0] \input ,
  input  reset,
  output [9:0] Output,
  output Negative_LED
);

  wire and_1_out, and_2_out, not_1_out, or_1_out, or_2_out;
  wire [9:0] negator_1_out;

  or or_1 (or_1_out, \input [9], \input [8], \input [7], \input [6], \input [5], \input [4], \input [3], \input [2], \input [1], \input [0]);
  and and_1 (and_1_out, \input [9], \input [8], \input [7], \input [6], \input [5], \input [4], \input [3], \input [2], \input [1], \input [0]);
  not not_1 (not_1_out, or_1_out);
  and and_2 (and_2_out, and_1_out, ~not_1_out);  // AND_Gate
  D_Flip_Flop d_ff_1 (.Q(Negative_LED), .preset(and_2_out), .reset(or_2_out));  // open: clk, D, Qn, en
  or or_2 (or_2_out, not_1_out, reset);
  Negator #(.width(10)) negator_1 (.in(\input ), .out(negator_1_out));
  Multiplexer #(.width(10)) multiplexer_1 (
    .in0(\input ), .in1(negator_1_out), .out(Output), .sel(Negative_LED));  // open: en
endmodule

module Directions (
  input  I,
  input  Reset,
  input  N,
  input  W,
  input  E,
  input  S,
  output [9:0] No,
  output [9:0] Wo,
  output [9:0] Eo,
  output [9:0] So
);

  tiny_director tiny_director_1 (.Increment(I), .direction(N), .Reset(Reset), .out_4(No));
  tiny_director tiny_director_2 (.Increment(I), .direction(W), .Reset(Reset), .out_4(Wo));
  tiny_director tiny_director_3 (.Increment(I), .direction(E), .Reset(Reset), .out_4(Eo));
  tiny_director tiny_director_4 (.Increment(I), .direction(S), .Reset(Reset), .out_4(So));
endmodule

module tiny_director (
  input  Increment,
  input  direction,
  input  Reset,
  output [9:0] out_4
);

  wire and_1_out, specific_counter_1_b1, specific_counter_1_b2, specific_counter_1_b3, specific_counter_1_b4,
       specific_counter_1_b5, specific_counter_1_b6, specific_counter_1_b7, specific_counter_1_b8,
       specific_counter_1_b9, specific_counter_1_b10;

  and and_1 (and_1_out, Increment, direction);
  Specific_counter specific_counter_1 (
    .a1(out_4[9]), .a2(out_4[8]), .a3(out_4[7]), .a4(out_4[6]), .a5(out_4[5]), .a6(out_4[4]), .a7(out_4[3]),
    .a8(out_4[2]), .a9(out_4[1]), .a10(out_4[0]), .b1(specific_counter_1_b1), .b2(specific_counter_1_b2),
    .b3(specific_counter_1_b3), .b4(specific_counter_1_b4), .b5(specific_counter_1_b5),
    .b6(specific_counter_1_b6), .b7(specific_counter_1_b7), .b8(specific_counter_1_b8),
    .b9(specific_counter_1_b9), .b10(specific_counter_1_b10));
  D_Flip_Flop d_ff_1 (.clk(and_1_out), .D(specific_counter_1_b1), .Q(out_4[9]), .reset(Reset));  // open: Qn, preset, en
  D_Flip_Flop d_ff_2 (.clk(and_1_out), .D(specific_counter_1_b2), .Q(out_4[8]), .reset(Reset));  // open: Qn, preset, en
  D_Flip_Flop d_ff_3 (.clk(and_1_out), .D(specific_counter_1_b3), .Q(out_4[7]), .reset(Reset));  // open: Qn, preset, en
  D_Flip_Flop d_ff_4 (.clk(and_1_out), .D(specific_counter_1_b4), .Q(out_4[6]), .reset(Reset));  // open: Qn, preset, en
  D_Flip_Flop d_ff_5 (.clk(and_1_out), .D(specific_counter_1_b6), .Q(out_4[4]), .reset(Reset));  // open: Qn, preset, en
  D_Flip_Flop d_ff_6 (.clk(and_1_out), .D(specific_counter_1_b5), .Q(out_4[5]), .reset(Reset));  // open: Qn, preset, en
  D_Flip_Flop d_ff_7 (.clk(and_1_out), .D(specific_counter_1_b8), .Q(out_4[2]), .reset(Reset));  // open: Qn, preset, en
  D_Flip_Flop d_ff_8 (.clk(and_1_out), .D(specific_counter_1_b7), .Q(out_4[3]), .reset(Reset));  // open: Qn, preset, en
  D_Flip_Flop d_ff_9 (.clk(and_1_out), .D(specific_counter_1_b9), .Q(out_4[1]), .reset(Reset));  // open: Qn, preset, en
  D_Flip_Flop d_ff_10 (
    .clk(and_1_out), .D(specific_counter_1_b10), .Q(out_4[0]), .reset(Reset));  // open: Qn, preset, en
endmodule

module Specific_counter (
  input  a1,
  input  a2,
  input  a3,
  input  a4,
  input  a5,
  input  a6,
  input  a7,
  input  a8,
  input  a9,
  input  a10,
  output b1,
  output b2,
  output b3,
  output b4,
  output b5,
  output b6,
  output b7,
  output b8,
  output b9,
  output b10
);

  wire and_1_out, and_2_out, and_3_out, and_4_out, and_5_out, and_6_out, and_7_out, and_8_out, and_9_out,
       and_10_out, and_11_out, and_12_out, and_13_out, and_14_out, and_15_out, and_16_out, and_17_out,
       and_18_out, and_19_out, and_20_out, and_21_out, and_22_out, and_23_out, and_24_out, and_25_out,
       and_26_out, and_27_out, and_28_out, and_29_out, and_30_out, and_31_out, and_32_out, and_33_out,
       and_34_out, and_35_out, and_36_out, and_37_out, and_38_out, and_39_out, and_40_out, and_41_out,
       and_42_out, and_43_out, and_44_out, and_45_out, and_46_out, and_47_out, and_48_out, and_49_out,
       and_50_out, and_51_out, and_52_out, and_53_out, and_54_out, not_1_out, not_2_out, not_3_out,
       not_4_out, not_5_out, not_6_out, not_7_out, not_8_out, not_9_out, not_10_out, not_11_out, not_12_out,
       not_13_out, not_14_out, not_15_out, not_16_out, not_17_out, not_18_out, not_19_out, not_20_out,
       not_21_out, not_22_out, not_23_out, not_24_out, not_25_out, not_26_out, not_27_out, not_28_out,
       not_29_out, not_30_out, not_31_out, not_32_out, not_33_out, not_34_out, not_35_out, not_36_out,
       not_37_out, not_38_out, not_39_out, not_40_out, not_41_out, not_42_out, not_43_out, not_44_out,
       not_45_out;

  and and_1 (and_1_out, a2, a3, a4, a5, a6, a7, a8, a9, a10);
  not not_1 (not_1_out, a2);
  not not_2 (not_2_out, a3);
  not not_3 (not_3_out, a4);
  not not_4 (not_4_out, a5);
  not not_5 (not_5_out, a6);
  not not_6 (not_6_out, a7);
  not not_7 (not_7_out, a8);
  not not_8 (not_8_out, a9);
  not not_9 (not_9_out, a10);
  not not_10 (not_10_out, a3);
  not not_11 (not_11_out, a4);
  not not_12 (not_12_out, a5);
  not not_13 (not_13_out, a6);
  not not_14 (not_14_out, a7);
  not not_15 (not_15_out, a8);
  not not_16 (not_16_out, a9);
  not not_17 (not_17_out, a10);
  not not_18 (not_18_out, a4);
  not not_19 (not_19_out, a5);
  not not_20 (not_20_out, a6);
  not not_21 (not_21_out, a7);
  not not_22 (not_22_out, a8);
  not not_23 (not_23_out, a9);
  not not_24 (not_24_out, a10);
  not not_25 (not_25_out, a5);
  not not_26 (not_26_out, a6);
  not not_27 (not_27_out, a7);
  not not_28 (not_28_out, a8);
  not not_29 (not_29_out, a9);
  not not_30 (not_30_out, a10);
  not not_31 (not_31_out, a6);
  not not_32 (not_32_out, a7);
  not not_33 (not_33_out, a8);
  not not_34 (not_34_out, a9);
  not not_35 (not_35_out, a10);
  not not_36 (not_36_out, a7);
  not not_37 (not_37_out, a8);
  not not_38 (not_38_out, a9);
  not not_39 (not_39_out, a10);
  not not_40 (not_40_out, a8);
  not not_41 (not_41_out, a9);
  not not_42 (not_42_out, a10);
  not not_43 (not_43_out, a9);
  not not_44 (not_44_out, a10);
  not not_45 (not_45_out, a10);
  and and_2 (and_2_out, a1, a2, a3, a4, a5, a6, a7, a8, a9);
  or or_1 (b1, and_1_out, a1);
  and and_3 (and_3_out, not_1_out, a3, a4, a5, a6, a7, a8, a9, a10);
  and and_4 (and_4_out, a2, not_2_out);
  and and_5 (and_5_out, a2, not_3_out);
  and and_6 (and_6_out, a2, not_4_out);
  and and_7 (and_7_out, a2, not_5_out);
  and and_8 (and_8_out, a2, not_6_out);
  and and_9 (and_9_out, a2, not_7_out);
  and and_10 (and_10_out, a2, not_8_out);
  and and_11 (and_11_out, a2, not_9_out);
  and and_12 (and_12_out, a1, a2);
  and and_13 (and_13_out, not_10_out, a4, a5, a6, a7, a8, a9, a10);
  and and_14 (and_14_out, a3, not_11_out);
  and and_15 (and_15_out, a3, not_12_out);
  and and_16 (and_16_out, a3, not_13_out);
  and and_17 (and_17_out, a3, not_14_out);
  and and_18 (and_18_out, a3, not_15_out);
  and and_19 (and_19_out, a3, not_16_out);
  and and_20 (and_20_out, a3, not_17_out);
  and and_21 (and_21_out, a1, a2, a3);
  and and_22 (and_22_out, not_18_out, a5, a6, a7, a8, a9, a10);
  and and_23 (and_23_out, a4, not_19_out);
  and and_24 (and_24_out, a4, not_20_out);
  and and_25 (and_25_out, a4, not_21_out);
  and and_26 (and_26_out, a4, not_22_out);
  and and_27 (and_27_out, a4, not_23_out);
  and and_28 (and_28_out, a4, not_24_out);
  and and_29 (and_29_out, a1, a2, a3, a4);
  and and_30 (and_30_out, not_25_out, a6, a7, a8, a9, a10);
  and and_31 (and_31_out, a5, not_26_out);
  and and_32 (and_32_out, a5, not_27_out);
  and and_33 (and_33_out, a5, not_28_out);
  and and_34 (and_34_out, a5, not_29_out);
  and and_35 (and_35_out, a5, not_30_out);
  and and_36 (and_36_out, a1, a2, a3, a4, a5);
  and and_37 (and_37_out, not_31_out, a7, a8, a9, a10);
  and and_38 (and_38_out, a6, not_32_out);
  and and_39 (and_39_out, a6, not_33_out);
  and and_40 (and_40_out, a6, not_34_out);
  and and_41 (and_41_out, a6, not_35_out);
  and and_42 (and_42_out, a1, a2, a3, a4, a5, a6);
  and and_43 (and_43_out, not_36_out, a8, a9, a10);
  and and_44 (and_44_out, a7, not_37_out);
  and and_45 (and_45_out, a7, not_38_out);
  and and_46 (and_46_out, a7, not_39_out);
  and and_47 (and_47_out, a1, a2, a3, a4, a5, a6, a7);
  and and_48 (and_48_out, not_40_out, a9, a10);
  and and_49 (and_49_out, a8, not_41_out);
  and and_50 (and_50_out, a8, not_42_out);
  and and_51 (and_51_out, a1, a2, a3, a4, a5, a6, a7, a8);
  and and_52 (and_52_out, not_43_out, a10);
  and and_53 (and_53_out, a9, not_44_out);
  and and_54 (and_54_out, a1, a2, a3, a4, a5, a6, a7, a8, a9);
  or or_2 (b10, not_45_out, and_2_out);
  or or_3 (b4, and_22_out, and_23_out, and_24_out, and_25_out, and_26_out, and_27_out, and_28_out, and_29_out);
  or or_4 (b5, and_30_out, and_31_out, and_32_out, and_33_out, and_34_out, and_35_out, and_36_out);
  or or_5 (b6, and_37_out, and_38_out, and_39_out, and_40_out, and_41_out, and_42_out);
  or or_6 (b7, and_43_out, and_44_out, and_45_out, and_46_out, and_47_out);
  or or_7 (b8, and_48_out, and_49_out, and_50_out, and_51_out);
  or or_8 (b9, and_52_out, and_53_out, and_54_out);
  or or_9 (b2, and_3_out, and_4_out, and_5_out, and_6_out, and_7_out, and_8_out, and_9_out, and_10_out, and_11_out, and_12_out);
  or or_10 (b3, and_13_out, and_14_out, and_15_out, and_16_out, and_17_out, and_18_out, and_19_out, and_20_out, and_21_out);
endmodule

module Totall_steps (
  input  [9:0] in_1,
  input  [9:0] in_2,
  input  [9:0] in_3,
  input  [9:0] in_4,
  output [11:0] out_5
);

  wire [9:0] adder_1_out, adder_2_out;
  wire [10:10] adder_1_cout, adder_2_cout;

  Adder #(.width(10)) adder_1 (.a(in_1), .b(in_2), .out(adder_1_out), .cout(adder_1_cout[10]));  // open: cin
  Adder #(.width(10)) adder_2 (.a(in_3), .b(in_4), .out(adder_2_out), .cout(adder_2_cout[10]));  // open: cin
  Adder #(.width(11)) adder_3 (
    .a({adder_1_cout[10], adder_1_out}), .b({adder_2_cout[10], adder_2_out}), .out(out_5[10:0]),
    .cout(out_5[11]));  // open: cin
endmodule

module timeout (
  input  Reset,
  input  Increment,
  input  n,
  input  W,
  input  e,
  input  s,
  output Warning
);

  wire clock_1_out, d_ff_1_q, d_ff_2_q, d_ff_3_q, d_ff_4_q, d_ff_5_q, d_ff_6_q, d_ff_7_q, d_ff_8_q, or_1_out,
       timeout_logic_1_s1, timeout_logic_1_s2, timeout_logic_1_s3, timeout_logic_1_s4, timeout_logic_1_s5,
       timeout_logic_1_s6, timeout_logic_1_s7, timeout_logic_1_s8;

  Clock clock_1 (.out(clock_1_out));
  or or_1 (or_1_out, Reset, Increment, n, W, e, s);
  and and_1 (Warning, d_ff_8_q, d_ff_7_q, d_ff_6_q, d_ff_5_q, d_ff_4_q, d_ff_3_q, d_ff_2_q, d_ff_1_q);
  D_Flip_Flop d_ff_1 (
    .clk(clock_1_out), .D(timeout_logic_1_s1), .Q(d_ff_1_q), .reset(or_1_out));  // open: Qn, preset, en
  Timeout_logic timeout_logic_1 (
    .a1(d_ff_1_q), .a2(d_ff_2_q), .a3(d_ff_3_q), .a4(d_ff_4_q), .a5(d_ff_5_q), .a6(d_ff_6_q), .a7(d_ff_7_q),
    .a8(d_ff_8_q), .s1(timeout_logic_1_s1), .s2(timeout_logic_1_s2), .s3(timeout_logic_1_s3),
    .s4(timeout_logic_1_s4), .s5(timeout_logic_1_s5), .s6(timeout_logic_1_s6), .s7(timeout_logic_1_s7),
    .s8(timeout_logic_1_s8));
  D_Flip_Flop d_ff_2 (
    .clk(clock_1_out), .D(timeout_logic_1_s2), .Q(d_ff_2_q), .reset(or_1_out));  // open: Qn, preset, en
  D_Flip_Flop d_ff_3 (
    .clk(clock_1_out), .D(timeout_logic_1_s3), .Q(d_ff_3_q), .reset(or_1_out));  // open: Qn, preset, en
  D_Flip_Flop d_ff_4 (
    .clk(clock_1_out), .D(timeout_logic_1_s4), .Q(d_ff_4_q), .reset(or_1_out));  // open: Qn, preset, en
  D_Flip_Flop d_ff_5 (
    .clk(clock_1_out), .D(timeout_logic_1_s5), .Q(d_ff_5_q), .reset(or_1_out));  // open: Qn, preset, en
  D_Flip_Flop d_ff_6 (
    .clk(clock_1_out), .D(timeout_logic_1_s6), .Q(d_ff_6_q), .reset(or_1_out));  // open: Qn, preset, en
  D_Flip_Flop d_ff_7 (
    .clk(clock_1_out), .D(timeout_logic_1_s7), .Q(d_ff_7_q), .reset(or_1_out));  // open: Qn, preset, en
  D_Flip_Flop d_ff_8 (
    .clk(clock_1_out), .D(timeout_logic_1_s8), .Q(d_ff_8_q), .reset(or_1_out));  // open: Qn, preset, en
endmodule

module Timeout_logic (
  input  a1,
  input  a2,
  input  a3,
  input  a4,
  input  a5,
  input  a6,
  input  a7,
  input  a8,
  output s1,
  output s2,
  output s3,
  output s4,
  output s5,
  output s6,
  output s7,
  output s8
);

  wire and_1_out, and_2_out, and_3_out, and_4_out, and_5_out, and_6_out, and_7_out, and_8_out, and_9_out,
       and_10_out, and_11_out, and_12_out, and_13_out, and_14_out, and_15_out, and_16_out, and_17_out,
       and_18_out, and_19_out, and_20_out, and_21_out, and_22_out, and_23_out, and_24_out, and_25_out,
       and_26_out, and_27_out, and_28_out, and_29_out, and_30_out, and_31_out, and_32_out, and_33_out,
       and_34_out, and_35_out, and_36_out, and_37_out, and_38_out, not_1_out, not_2_out, not_3_out,
       not_4_out, not_5_out, not_6_out, not_7_out, not_8_out, not_9_out, not_10_out, not_11_out, not_12_out,
       not_13_out, not_14_out, not_15_out, not_16_out, not_17_out, not_18_out, not_19_out, not_20_out,
       not_21_out;

  and and_1 (and_1_out, a2, a3, a6);
  and and_2 (and_2_out, a2, a3, a5);
  and and_3 (and_3_out, a2, a3, a4);
  and and_4 (and_4_out, a3, a4, a5, a6, a7, a8);
  not not_1 (not_1_out, a3);
  not not_2 (not_2_out, a4);
  not not_3 (not_3_out, a5);
  not not_4 (not_4_out, a6);
  not not_5 (not_5_out, a7);
  not not_6 (not_6_out, a8);
  not not_7 (not_7_out, a4);
  not not_8 (not_8_out, a5);
  not not_9 (not_9_out, a6);
  not not_10 (not_10_out, a7);
  not not_11 (not_11_out, a8);
  not not_12 (not_12_out, a5);
  not not_13 (not_13_out, a6);
  not not_14 (not_14_out, a7);
  not not_15 (not_15_out, a8);
  not not_16 (not_16_out, a6);
  and and_5 (and_5_out, not_16_out, a7, a8);
  and and_6 (and_6_out, a6, not_17_out);
  not not_17 (not_17_out, a7);
  and and_7 (and_7_out, a6, not_18_out);
  not not_18 (not_18_out, a8);
  and and_8 (and_8_out, a2, a3, a6);
  and and_9 (and_9_out, a2, a3, a5);
  and and_10 (and_10_out, a2, a3, a4);
  not not_19 (not_19_out, a7);
  and and_11 (and_11_out, not_19_out, a8);
  and and_12 (and_12_out, a7, not_20_out);
  not not_20 (not_20_out, a8);
  and and_13 (and_13_out, a2, a3, a6);
  and and_14 (and_14_out, a2, a3, a5);
  and and_15 (and_15_out, a2, a3, a4);
  not not_21 (not_21_out, a8);
  and and_16 (and_16_out, a2, a3, a6);
  and and_17 (and_17_out, a2, a3, a5);
  and and_18 (and_18_out, a2, a3, a4);
  or or_1 (s1, and_1_out, and_2_out, and_3_out, a1);
  or or_2 (s2, and_4_out, a2, a1);
  and and_19 (and_19_out, not_1_out, a4, a5, a6, a7, a8);
  and and_20 (and_20_out, a3, not_2_out);
  and and_21 (and_21_out, a3, not_3_out);
  and and_22 (and_22_out, a3, not_4_out);
  and and_23 (and_23_out, a3, not_5_out);
  and and_24 (and_24_out, a3, not_6_out);
  and and_25 (and_25_out, a2, a3);
  and and_26 (and_26_out, not_7_out, a5, a6, a7, a8);
  and and_27 (and_27_out, a4, not_8_out);
  and and_28 (and_28_out, a4, not_9_out);
  and and_29 (and_29_out, a4, not_10_out);
  and and_30 (and_30_out, a4, not_11_out);
  and and_31 (and_31_out, a2, a3, a6);
  and and_32 (and_32_out, a2, a3, a5);
  and and_33 (and_33_out, not_12_out, a6, a7, a8);
  and and_34 (and_34_out, a5, not_13_out);
  and and_35 (and_35_out, a5, not_14_out);
  and and_36 (and_36_out, a5, not_15_out);
  and and_37 (and_37_out, a2, a3, a6);
  and and_38 (and_38_out, a2, a3, a4);
  or or_3 (s8, not_21_out, and_16_out, and_17_out, and_18_out, a1);
  or or_4 (s3, and_19_out, and_20_out, and_21_out, and_22_out, and_23_out, and_24_out, and_25_out, a1);
  or or_5 (s4, and_26_out, and_27_out, and_28_out, and_29_out, and_30_out, and_31_out, and_32_out, a1);
  or or_6 (s5, and_33_out, and_34_out, and_35_out, and_36_out, and_37_out, and_38_out, a1);
  or or_7 (s6, and_5_out, and_6_out, and_7_out, and_8_out, and_9_out, and_10_out, a1);
  or or_8 (s7, and_11_out, and_12_out, and_13_out, and_14_out, and_15_out, a1);
endmodule

module dumb_controls (
  input  Reset,
  input  stay,
  input  turnleft,
  input  turnright,
  input  turnaround,
  output n,
  output w,
  output e,
  output s
);

  dumblogic dumblogic_1 (
    .stay(stay), .turnleft(turnleft), .turnright(turnright), .turnaround(turnaround), .Reset(Reset), .N(n),
    .W(w), .E(e), .S(s));
endmodule

module dumblogic (
  input  Reset,
  input  stay,
  input  turnleft,
  input  turnright,
  input  turnaround,
  output N,
  output W,
  output E,
  output S
);

  wire c_q, d_q, dumb_tiny_math_1_c, dumb_tiny_math_1_d, not_1_out, or_1_out;

  dumb_tiny_math dumb_tiny_math_1 (
    .stay(stay), .turnleft(turnleft), .turnright(turnright), .turnaround(turnaround), .a(c_q), .b(d_q),
    .c(dumb_tiny_math_1_c), .d(dumb_tiny_math_1_d));
  not not_1 (not_1_out, or_1_out);
  or or_1 (or_1_out, stay, turnleft, turnright, turnaround);
  D_Flip_Flop d (.clk(not_1_out), .D(dumb_tiny_math_1_d), .Q(d_q), .reset(Reset));  // open: Qn, preset, en
  D_Flip_Flop c (.clk(not_1_out), .D(dumb_tiny_math_1_c), .Q(c_q), .reset(Reset));  // open: Qn, preset, en
  cardinal_finder cardinal_finder_1 (.C(c_q), .D(d_q), .n(N), .w(W), .e(E), .s(S));
endmodule

module dumb_tiny_math (
  input  stay,
  input  turnleft,
  input  turnright,
  input  turnaround,
  input  a,
  input  b,
  output c,
  output d
);

  wire and_1_out, and_2_out, and_3_out, and_4_out, and_5_out, and_6_out, and_7_out, and_8_out, and_9_out,
       and_10_out, not_1_out, not_2_out, not_3_out, not_4_out, not_5_out, not_6_out, not_7_out, not_8_out,
       not_9_out, not_10_out, not_11_out, not_12_out, not_13_out;

  not not_1 (not_1_out, turnleft);
  not not_2 (not_2_out, turnright);
  not not_3 (not_3_out, turnaround);
  not not_4 (not_4_out, a);
  not not_5 (not_5_out, b);
  not not_6 (not_6_out, a);
  not not_7 (not_7_out, turnleft);
  not not_8 (not_8_out, turnright);
  not not_9 (not_9_out, turnaround);
  not not_10 (not_10_out, b);
  not not_11 (not_11_out, a);
  not not_12 (not_12_out, turnaround);
  not not_13 (not_13_out, a);
  and and_1 (and_1_out, not_1_out, not_2_out, not_3_out, a);
  and and_2 (and_2_out, turnaround, not_4_out);
  and and_3 (and_3_out, turnright, not_5_out);
  and and_4 (and_4_out, turnleft, b);
  and and_5 (and_5_out, stay, turnright, not_6_out);
  and and_6 (and_6_out, not_7_out, not_8_out, not_9_out, b);
  and and_7 (and_7_out, turnaround, not_10_out);
  and and_8 (and_8_out, turnright, a);
  and and_9 (and_9_out, turnleft, not_11_out);
  and and_10 (and_10_out, stay, not_12_out, not_13_out, b);
  or or_1 (c, and_1_out, and_2_out, and_3_out, and_4_out, and_5_out);
  or or_2 (d, and_6_out, and_7_out, and_8_out, and_9_out, and_10_out);
endmodule

module cardinal_finder (
  input  C,
  input  D,
  output n,
  output w,
  output e,
  output s
);

  wire not_1_out, not_2_out, not_3_out, not_4_out;

  not not_1 (not_1_out, C);
  not not_2 (not_2_out, D);
  and and_1 (s, C, D);
  not not_3 (not_3_out, D);
  not not_4 (not_4_out, C);
  and and_2 (n, not_1_out, not_2_out);
  and and_3 (e, C, not_3_out);
  and and_4 (w, not_4_out, D);
endmodule

module GPS2_0 (
  output [9:0] Y___Axis,
  output [9:0] X___Axis,
  output [9:0] North,
  output [9:0] west,
  output [9:0] East,
  output [9:0] South,
  output [11:0] Total
);

  wire dumblogic_1_e, dumblogic_1_n, dumblogic_1_s, dumblogic_1_w, main_1_e_2, main_1_n_2, main_1_s_2,
       main_1_w_2, Reset_On_out, signer_1_negative_led, signer_2_negative_led, Stay_out, Take_step_out,
       timeout_1_warning, Turn_Around_out, Turn_Left_out, Turn_Right_out;
  wire [9:0] main_1_y_axis, main_1_y_axis_2;

  Button Reset_On (.out(Reset_On_out));
  Button Turn_Left (.out(Turn_Left_out));
  Button Take_step (.out(Take_step_out));
  Button Stay (.out(Stay_out));
  Button Turn_Right (.out(Turn_Right_out));
  Button Turn_Around (.out(Turn_Around_out));
  timeout timeout_1 (
    .Reset(Reset_On_out), .Increment(Turn_Around_out), .n(Take_step_out), .W(Stay_out), .e(Turn_Left_out),
    .s(Turn_Right_out), .Warning(timeout_1_warning));
  dumblogic dumblogic_1 (
    .stay(Stay_out), .turnleft(Turn_Left_out), .turnright(Turn_Right_out), .turnaround(Turn_Around_out),
    .Reset(Reset_On_out), .N(dumblogic_1_n), .W(dumblogic_1_w), .E(dumblogic_1_e), .S(dumblogic_1_s));
  LED N (.in(main_1_n_2));
  LED W (.in(main_1_w_2));
  LED S (.in(main_1_s_2));
  main main_1 (
    .N(dumblogic_1_n), .W(dumblogic_1_w), .E(dumblogic_1_e), .S(dumblogic_1_s), .Reset(Reset_On_out),
    .Increment(Take_step_out), .N_2(main_1_n_2), .W_2(main_1_w_2), .E_2(main_1_e_2), .S_2(main_1_s_2),
    .y_axis(main_1_y_axis), .y_axis_2(main_1_y_axis_2), .North(North), .Total_Steps(Total), .West(west),
    .East(East), .South(South));
  LED E (.in(main_1_e_2));
  LED Warning_LED (.in(timeout_1_warning));
  signer signer_1 (
    .\input (main_1_y_axis), .reset(Reset_On_out), .Output(Y___Axis), .Negative_LED(signer_1_negative_led));
  LED Negative (.in(signer_1_negative_led));
  LED Negative_2 (.in(signer_2_negative_led));
  signer signer_2 (
    .\input (main_1_y_axis_2), .reset(Reset_On_out), .Output(X___Axis), .Negative_LED(signer_2_negative_led));

  // Notes on the sheet:
  //   7 sec
endmodule
